# Fritzing sketch winder layout Ivar og Kjetil (saved by Fritzing 0.9.0b)
circuit board: 6.9215cm x 5.33756cm
breadboards: 1

parts:
  IC1 = L293D [package=THT]
  Part1 = Arduino Uno (Rev3)
  J1 = Screw terminal - 2 pins [package=THT]
  J2 = screw terminal, 4 pins
  JACK1 = 2.1mm DC Barrel Jack
  C1 = Electrolytic Capacitor [capacitance=1µF package="100 mil [THT, electrolytic]"]
  R1 = Resistor [tolerance=±5% resistance=220 package=THT]
  R2 = Resistor [tolerance=±5% resistance=100 package=THT]
  U1 = POT [package=pot_alpha_rv16af-20]
  U2 = 555 Timer [part_number="pwm generator" package="SO8 [SMD]"]
  IC2 = L293D [part_number="rotation controller" package=THT]
  Part2 = Arduino Uno (Rev3)
  U3 = POT [part_number="rotation speed" package=pot_alpha_rv16af-20]  # not connected
  JACK2 = 2.1mm Barrel Jack with Terminal Block [part_number="12 v 2.1 mm input"]
  M1 = DC Motor [part_number="12 V DC Motor - 1000 rpm geared"]
  IC3 = L293D [part_number="traverse controller" package=THT]
  M2 = Stepper Motor - Bipolar
  C2 = Electrolytic Capacitor [capacitance=1µF package="100 mil [THT, electrolytic]"]
  U4 = Voltage Regulator [part_number="lm317 12v to 5v regulator" package=to220-adj]
  R4 = Resistor [tolerance=±5% resistance=720 package=THT]
  R5 = Resistor [tolerance=±5% resistance=720 package=THT]
  C3 = Electrolytic Capacitor [capacitance=1µF package="100 mil [THT, electrolytic]"]
  C5 = Capacitor [part_number="0.1 uf" package=cap-pth-5mm]
  J3 = Screw terminal - 2 pins [package=THT]  # not connected
  J6 = Screw terminal - 5 pins [part_number="I2C BACKPACK" package=THT]

nets (from the schematic view):
  N1: IC1.Enable_1, Part1.D3_PWM
  N2: IC1.In_1, Part1.D6_PWM
  N3: IC1.Out_1_(_Controlled_by_Enable_1_), J1.pin2
  N4: IC1.0V, Part1.GND, JACK1.sleeve, C1.-, U1.E
  N5: IC1.Out_2_(_Controlled_by_Enable_1_), J1.pin1
  N6: IC1.In_2, Part1.D2
  N7: IC1.+Vmotor, JACK1.center, C1.+
  N8: Part1.A0, J2.pin1, R1.Pin_0
  N9: Part1.A1, U1.S
  N10: Part1.5V, J2.pin4, U1.A
  N11: J2.pin2, R2.Pin_1
  N12: J2.pin3, R1.Pin_1
  N13: U2.Pin_7, IC2.Enable_1
  N14: IC2.In_1, Part2.D2
  N15: IC2.Out_1_(_Controlled_by_Enable_1_), M1.pin_1
  N16: IC2.0V, IC3.0V
  N17: IC2.Out_2_(_Controlled_by_Enable_1_), M1.pin_2
  N18: IC2.In_2, Part2.D7
  N19: IC2.+Vmotor, C2.-
  GND: Part2.GND, JACK2.NEG, R4.Pin_1, C3.-, C5.2, J6.GND
  5V: Part2.5V, J6.5V
  N20: Part2.VIN, U4.OUT, R5.Pin_0, C3.+
  N21: JACK2.POS, IC3.+Vmotor, C2.+, U4.IN, C5.1
  N22: IC3.Out_1_(_Controlled_by_Enable_1_), M2.C
  N23: IC3.Out_2_(_Controlled_by_Enable_1_), M2.A
  N24: IC3.Out_3_(_Controlled_by_Enable_2_), M2.D
  N25: IC3.Out_4_(_Controlled_by_Enable_2_), M2.B
  N26: U4.ADJ, R4.Pin_0, R5.Pin_1

custom parts:
  2.1mm DC Barrel Jack: 2.1mm DC Barrel Jack with Thru-Hole Connectors (breadboardable)
  Screw terminal - 5 pins: Screw terminal with 5 pins
